# Fritzing sketch arduino_boot_menu_usb_keyboard (saved by Fritzing 0.9.3b)
breadboards: 1

parts:
  Part1 = Arduino Pro Mini v13
  S1 = Pushbutton [package="[THT]"]
  S2 = Pushbutton [package="[THT]"]
  S3 = Pushbutton [package="[THT]"]
  S4 = Pushbutton [package="[THT]"]

nets:
  N1: Part1.GND, S1.Pin_1, S1.Pin_2, S2.Pin_1, S2.Pin_2, S3.Pin_1, S3.Pin_2, S4.Pin_1, S4.Pin_2
  N2: Part1.D5_PWM, S4.Pin_3, S4.Pin_4
  N3: Part1.D4, S3.Pin_3, S3.Pin_4
  N4: Part1.D3_PWM, S2.Pin_3, S2.Pin_4
  N5: Part1.D2, S1.Pin_3, S1.Pin_4
